# Fritzing sketch MQ131_Arduino_Uno_circuit (saved by Fritzing 0.9.3b)
breadboards: 1

parts:
  Part1 = Arduino Uno (Rev3)
  Q1 = Basic FET N-Channel [part_number=IRF840 package="TO220 [THT]"]
  U1 = GAS_SENSOR [part_number=MQ131 package=mq-3]
  R1 = Resistor [tolerance=±5% resistance=1M package=THT]

nets:
  N1: Part1.A0, U1.B1, R1.Pin_0
  N2: Part1.GND, Q1.source, R1.Pin_1
  N3: Part1.D2, Q1.gate
  N4: Part1.5V, U1.A1, U1.H1
  N5: Q1.drain, U1.H2

notes:
  MQ131
  Sensor circuit
  Heater circuit
